# Fritzing sketch SistemaArmazenamentoCaptacaoChuva (saved by Fritzing 0.9.2b)
circuit board: 8.46667cm x 5.64444cm
breadboards: 1

parts:
  Componente3 = Arduino Uno (Rev3)
  J1 = Basic Servo
  U3 = HC-SR04 [chip_label=IC package="SIP (Single Inline) [THT]"]
  U4 = HC-SR04 [chip_label=IC package="SIP (Single Inline) [THT]"]  # not connected
  YL-83_-_Detection_Board1 = YL-83 Rain Sensor - Detection Board
  YL-83_-_Control_Board1 = YL-83 Rain Sensor - Control Board

nets:
  N1: Componente3.A3, YL-83_-_Control_Board1.AO
  N2: Componente3.D2, J1.pulse
  N3: Componente3.D7, U3.Trig, U3.Echo
  VCC: Componente3.5V, J1.vcc, U3.Vcc, YL-83_-_Control_Board1.VCC
  GND: Componente3.GND, J1.gnd, U3.GND, YL-83_-_Control_Board1.GND
  N4: YL-83_-_Detection_Board1.POS, YL-83_-_Control_Board1.POS
  N5: YL-83_-_Detection_Board1.NEG, YL-83_-_Control_Board1.NEG

custom parts:
  HC-SR04: HC-SR04 ultrasound distance sensor
  YL-83 Rain Sensor - Detection Board: The YL-83 is a rain sensor that has more resistance when dry and less resistance when wet. The module runs at 5V.
  YL-83 Rain Sensor - Control Board: The YL-83 is a rain sensor that has more resistance when dry and less resistance when wet. The module runs at 5V.
