# Fritzing sketch rainSensor (saved by Fritzing 0.9.2b)
circuit board: 8.46667cm x 5.64444cm
breadboards: 1

parts:
  YL-83_-_Control_Board1 = YL-83 Rain Sensor - Control Board
  YL-83_-_Detection_Board1 = YL-83 Rain Sensor - Detection Board
  U3 = HC-SR04 [chip_label=IC package="SIP (Single Inline) [THT]"]
  Componente3 = Arduino Uno (Rev3)
  U4 = HC-SR04 [chip_label=IC package="SIP (Single Inline) [THT]"]  # not connected
  J1 = Basic Servo  # not connected

nets:
  VCC: YL-83_-_Control_Board1.VCC, U3.Vcc, Componente3.5V
  N1: YL-83_-_Control_Board1.POS, YL-83_-_Detection_Board1.POS
  N2: YL-83_-_Control_Board1.NEG, YL-83_-_Detection_Board1.NEG
  N3: U3.Trig, U3.Echo, Componente3.D7
  GND: U3.GND, Componente3.GND

custom parts:
  YL-83 Rain Sensor - Control Board: The YL-83 is a rain sensor that has more resistance when dry and less resistance when wet. The module runs at 5V.
  YL-83 Rain Sensor - Detection Board: The YL-83 is a rain sensor that has more resistance when dry and less resistance when wet. The module runs at 5V.
  HC-SR04: HC-SR04 ultrasound distance sensor
